// Logisim project checkers.circ as structural Verilog: 3 circuits, main circuit main
module main (
);

  wire clock_1_out, Manual_Reset_out, reset, rgb_video_1_p1, rgb_video_1_p3;
  wire [2:0] X, Y;
  wire [4:0] entrada;
  wire [23:0] cor;

  // Rv32im #(.SocBusSelection('h0000019386873D0349eb52fa)) rv32im_1: pin names not known
  Clock clock_1 (.out(clock_1_out));
  // SocBus #(.SocBusIdentifier('h0000019386873D0349eb52fa)) socbus_1: pin names not known; wires that end beside it: reset, clock_1_out
  // Socmem #(.SocBusSelection('h0000019386873D0349eb52fa)) memoria: pin names not known
  // SocPio #(.SocBusSelection('h0000019386873D0349eb52fa), .StartAddress('h460), .direction("outputonly")) reset: pin names not known
  // SocPio #(.SocBusSelection('h0000019386873D0349eb52fa), .StartAddress('h400), .direction("outputonly"), .width(3)) saida_x: pin names not known
  // SocPio #(.SocBusSelection('h0000019386873D0349eb52fa), .StartAddress('h418), .direction("outputonly"), .width(3)) saida_y: pin names not known
  // SocPio #(.SocBusSelection('h0000019386873D0349eb52fa), .StartAddress('h430), .direction("outputonly"), .width(24)) cor: pin names not known; wires that end beside it: cor[23], cor[22], cor[21], cor[20], cor[19], cor[18], cor[17], cor[16], cor[15], cor[14], cor[13]
  // SocPio #(.SocBusSelection('h0000019386873D0349eb52fa), .StartAddress('h448), .width(5)) entrada: pin names not known
  Button Manual_Reset (.out(Manual_Reset_out));
  joystick_ctrl joystick_ctrl_1 (.Q(entrada[4]), .E(entrada[3]), .A(entrada[2]), .D(entrada[1]));  // open: X, Y
  or or_1 (reset, Manual_Reset_out, rgb_video_1_p1);
  Button OK (.out(entrada[0]));
  Joystick joystick_1 ();  // open: x, y
  // RGB_Video #(.height(8), .scale(8), .width(8)) rgb_video_1: pin names not known; wires that end beside it: rgb_video_1_p1, reset, rgb_video_1_p3, 1'b1, X, Y, cor
  Clock clock_2 (.out(rgb_video_1_p3));
endmodule

// 4x
module upscaler (
  input  [2:0] x,
  input  [2:0] y,
  output [4:0] x4,
  output [4:0] y4
);


  assign x4 = {x, 2'b00};
  assign y4 = {y, 2'b00};
endmodule

// ctrl
module joystick_ctrl (
  input  [3:0] X,
  input  [3:0] Y,
  output Q,
  output E,
  output A,
  output D
);

  wire and_1_out, and_2_out, comparator_1_gt, comparator_1_lt, comparator_2_gt, comparator_2_lt,
       demultiplexer_1_out0, demultiplexer_1_out1, demultiplexer_2_out0, demultiplexer_2_out1,
       multiplexer_1_out, multiplexer_2_out, multiplexer_3_out, multiplexer_4_out;

  and and_1 (and_1_out, ~X[0], ~X[1], ~X[2]);  // AND_Gate
  Comparator #(.mode("unsigned"), .width(3)) comparator_1 (
    .a(X[2:0]), .b(3'b100), .gt(comparator_1_gt), .lt(comparator_1_lt));  // open: eq
  and and_2 (and_2_out, ~Y[0], ~Y[1], ~Y[2]);  // AND_Gate
  Comparator #(.mode("unsigned"), .width(3)) comparator_2 (
    .a(Y[2:0]), .b(3'b100), .gt(comparator_2_gt), .lt(comparator_2_lt));  // open: eq
  Multiplexer multiplexer_1 (.in0(comparator_1_lt), .in1(comparator_1_gt), .out(multiplexer_1_out), .sel(X[3]));
  Demultiplexer demultiplexer_1 (
    .out0(demultiplexer_1_out0), .out1(demultiplexer_1_out1), .in(multiplexer_2_out), .sel(X[3]));
  Multiplexer multiplexer_2 (.in0(multiplexer_1_out), .in1(1'b0), .out(multiplexer_2_out), .sel(and_1_out));
  Multiplexer multiplexer_3 (.in0(comparator_2_lt), .in1(comparator_2_gt), .out(multiplexer_3_out), .sel(Y[3]));
  Demultiplexer demultiplexer_2 (
    .out0(demultiplexer_2_out0), .out1(demultiplexer_2_out1), .in(multiplexer_4_out), .sel(Y[3]));
  Multiplexer multiplexer_4 (.in0(multiplexer_3_out), .in1(1'b0), .out(multiplexer_4_out), .sel(and_2_out));
  and and_3 (Q, demultiplexer_1_out0, demultiplexer_2_out0);
  and and_4 (E, demultiplexer_1_out1, demultiplexer_2_out0);
  and and_5 (A, demultiplexer_1_out0, demultiplexer_2_out1);
  and and_6 (D, demultiplexer_1_out1, demultiplexer_2_out1);

  // Notes on the sheet:
  //   left
  //   right
  //   up
  //   down
endmodule
